// Logisim project ObligatorioArquitecturaDeSistemas.circ as structural Verilog: 11 circuits, main circuit Main
module Movimiento_auto (
  input  in_1,
  input  [7:0] in_2,
  input  [7:0] in_3,
  input  [7:0] in_4,
  input  [7:0] in_5,
  output [7:0] out_6,
  output [7:0] out_7,
  output [7:0] out_8,
  output [7:0] out_9
);

  wire [2:0] register_1_q, register_2_q, register_3_q;
  wire [7:0] multiplexer_1_out, multiplexer_2_out, multiplexer_3_out, multiplexer_4_out, shifter_1_out,
       shifter_2_out, shifter_3_out, shifter_4_out, shifter_5_out, shifter_6_out, shifter_7_out,
       shifter_8_out;

  Shifter #(.shift("lr")) shifter_1 (.in(8'h20), .\dist (3'b011), .out(shifter_1_out));
  Shifter #(.shift("lr")) shifter_2 (.in(8'h70), .\dist (3'b011), .out(shifter_2_out));
  Shifter #(.shift("lr")) shifter_3 (.in(8'h20), .\dist (3'b011), .out(shifter_3_out));
  Shifter #(.shift("lr")) shifter_4 (.in(8'h50), .\dist (3'b011), .out(shifter_4_out));
  Shifter shifter_5 (.in(8'h20), .\dist (register_1_q), .out(shifter_5_out));
  Register #(.width(3)) register_1 (.Q(register_1_q));  // open: D, en, clk, clr
  Shifter shifter_6 (.in(8'h70), .\dist (register_1_q), .out(shifter_6_out));
  Shifter shifter_7 (.in(8'h20), .\dist (register_2_q), .out(shifter_7_out));
  Register #(.width(3)) register_2 (.Q(register_2_q));  // open: D, en, clk, clr
  Shifter shifter_8 (.in(8'h50), .\dist (register_3_q), .out(shifter_8_out));
  Register #(.width(3)) register_3 (.Q(register_3_q));  // open: D, en, clk, clr
  Multiplexer #(.width(8)) multiplexer_1 (
    .in0(shifter_5_out), .in1(shifter_1_out), .out(multiplexer_1_out), .sel(in_1));  // open: en
  Multiplexer #(.width(8)) multiplexer_2 (
    .in0(shifter_6_out), .in1(shifter_2_out), .out(multiplexer_2_out), .sel(in_1));  // open: en
  Multiplexer #(.width(8)) multiplexer_3 (
    .in0(shifter_7_out), .in1(shifter_3_out), .out(multiplexer_3_out), .sel(in_1));  // open: en
  Multiplexer #(.width(8)) multiplexer_4 (
    .in0(shifter_8_out), .in1(shifter_4_out), .out(multiplexer_4_out), .sel(in_1));  // open: en
  Adder adder_1 (.a(multiplexer_2_out), .b(in_3), .out(out_7));  // open: cin, cout
  Adder adder_2 (.a(multiplexer_1_out), .b(in_2), .out(out_6));  // open: cin, cout
  Adder adder_3 (.a(multiplexer_3_out), .b(in_4), .out(out_8));  // open: cin, cout
  Adder adder_4 (.a(multiplexer_4_out), .b(in_5), .out(out_9));  // open: cin, cout
endmodule

module Grupo_Registros (
  input  [7:0] in_1,
  input  in_2,
  input  in_3,
  output [7:0] out_4,
  output [7:0] out_5,
  output [7:0] out_6,
  output [7:0] out_7,
  output [7:0] out_8,
  output [7:0] out_9,
  output [7:0] out_10,
  output [7:0] out_11,
  output [7:0] out_12,
  output [7:0] out_13,
  output [7:0] out_14,
  output [7:0] out_15,
  output [7:0] out_16,
  output [7:0] out_17
);

  wire not_1_out;

  not not_1 (not_1_out, in_3);
  Register register_1 (.D(in_1), .Q(out_4), .clk(in_2), .clr(not_1_out));  // open: en
  Register register_2 (.D(out_4), .Q(out_5), .clk(in_2), .clr(not_1_out));  // open: en
  Register register_3 (.D(out_6), .Q(out_7), .clk(in_2), .clr(not_1_out));  // open: en
  Register register_4 (.D(out_5), .Q(out_6), .clk(in_2), .clr(not_1_out));  // open: en
  Register register_5 (.D(out_7), .Q(out_8), .clk(in_2), .clr(not_1_out));  // open: en
  Register register_6 (.D(out_8), .Q(out_9), .clk(in_2), .clr(not_1_out));  // open: en
  Register register_7 (.D(out_9), .Q(out_10), .clk(in_2), .clr(not_1_out));  // open: en
  Register register_8 (.D(out_10), .Q(out_11), .clk(in_2), .clr(not_1_out));  // open: en
  Register register_9 (.D(out_11), .Q(out_12), .clk(in_2), .clr(not_1_out));  // open: en
  Register register_10 (.D(out_13), .Q(out_14), .clk(in_2), .clr(not_1_out));  // open: en
  Register register_11 (.D(out_15), .Q(out_16), .clk(in_2), .clr(not_1_out));  // open: en
  Register register_12 (.D(out_12), .Q(out_13), .clk(in_2), .clr(not_1_out));  // open: en
  Register register_13 (.D(out_14), .Q(out_15), .clk(in_2), .clr(not_1_out));  // open: en
  Register register_14 (.D(out_16), .Q(out_17), .clk(in_2), .clr(not_1_out));  // open: en
endmodule

module Score (
  input  [7:0] in_1,
  input  in_2,
  input  in_3,
  output out_4,
  output out_5,
  output out_6,
  output out_7,
  output out_8
);

  wire and_1_out, and_2_out, and_3_out, and_4_out, and_5_out, comparator_1_eq, comparator_2_eq,
       comparator_3_eq, comparator_4_eq, controlled_buffer_1_out, counter_1_carry, d_ff_1_q, d_ff_2_qn,
       d_ff_3_q, d_ff_4_qn, not_1_out, not_2_out, or_1_out;
  wire [2:0] counter_1_q;
  wire [7:0] register_1_q, register_2_q, register_3_q, register_4_q, register_5_q, register_6_q,
       register_7_q, rom_1_data;

  Counter #(.width(3), .max('h7), .ongoal("stay")) counter_1 (
    .Q(counter_1_q), .carry(counter_1_carry), .clk(in_2));  // open: load, D, count, clr
  not not_1 (not_1_out, in_3);
  not not_2 (not_2_out, counter_1_carry);
  assign controlled_buffer_1_out = not_2_out ? in_2 : 1'bz;  // Controlled_Buffer controlled_buffer_1
  ROM #(.addrWidth(3)) rom_1 (.addr(counter_1_q), .data(rom_1_data));  // open: sel
  Register register_1 (.D(rom_1_data), .Q(register_1_q), .clk(controlled_buffer_1_out));  // open: en, clr
  Comparator comparator_1 (.a(in_1), .b(register_4_q), .eq(comparator_1_eq));  // open: gt, lt
  Comparator comparator_2 (.a(in_1), .b(register_5_q), .eq(comparator_2_eq));  // open: gt, lt
  Comparator comparator_3 (.a(in_1), .b(register_6_q), .eq(comparator_3_eq));  // open: gt, lt
  Comparator comparator_4 (.a(in_1), .b(register_7_q), .eq(comparator_4_eq));  // open: gt, lt
  Register register_2 (.D(register_1_q), .Q(register_2_q), .clk(controlled_buffer_1_out));  // open: en, clr
  D_Flip_Flop d_ff_1 (.clk(in_2), .D(comparator_1_eq), .Q(d_ff_1_q));  // open: Qn, preset, en, reset
  D_Flip_Flop d_ff_2 (.clk(in_2), .D(comparator_2_eq), .Qn(d_ff_2_qn));  // open: Q, preset, en, reset
  D_Flip_Flop d_ff_3 (.clk(in_2), .D(comparator_3_eq), .Q(d_ff_3_q));  // open: Qn, preset, en, reset
  D_Flip_Flop d_ff_4 (.clk(in_2), .D(comparator_4_eq), .Qn(d_ff_4_qn));  // open: Q, preset, en, reset
  Register register_3 (.D(register_2_q), .Q(register_3_q), .clk(controlled_buffer_1_out));  // open: en, clr
  and and_1 (and_1_out, d_ff_1_q, d_ff_2_qn);
  and and_2 (and_2_out, d_ff_3_q, d_ff_4_qn);
  Register register_4 (.D(register_3_q), .Q(register_4_q), .clk(controlled_buffer_1_out));  // open: en, clr
  or or_1 (or_1_out, and_1_out, and_2_out);
  Register register_5 (.D(register_4_q), .Q(register_5_q), .clk(controlled_buffer_1_out));  // open: en, clr
  Register register_6 (.D(register_5_q), .Q(register_6_q), .clk(controlled_buffer_1_out));  // open: en, clr
  and and_3 (and_3_out, out_4, or_1_out);
  J_K_Flip_Flop j_k_ff_1 (
    .J(or_1_out), .clk(in_2), .K(or_1_out), .Q(out_4), .reset(not_1_out));  // open: Qn, preset, en
  Register register_7 (.D(register_6_q), .Q(register_7_q), .clk(controlled_buffer_1_out));  // open: en, clr
  and and_4 (and_4_out, out_5, and_3_out);
  J_K_Flip_Flop j_k_ff_2 (
    .J(and_3_out), .clk(in_2), .K(and_3_out), .Q(out_5), .reset(not_1_out));  // open: Qn, preset, en
  and and_5 (and_5_out, out_6, and_4_out);
  J_K_Flip_Flop j_k_ff_3 (
    .J(and_4_out), .clk(in_2), .K(and_4_out), .Q(out_6), .reset(not_1_out));  // open: Qn, preset, en
  and and_6 (out_8, out_7, and_5_out);
  J_K_Flip_Flop j_k_ff_4 (
    .J(and_5_out), .clk(in_2), .K(and_5_out), .Q(out_7), .reset(not_1_out));  // open: Qn, preset, en

  // Notes on the sheet:
  //   contents of rom_1 (hex, n*v repeats v):
  //   d1 d5 8b ab
endmodule

module Choques (
  input  in_1,
  input  [7:0] in_2,
  input  in_3,
  input  [7:0] in_4,
  output out_5,
  output out_6,
  output out_7
);

  wire and_1_out, and_2_out, comparator_1_eq, comparator_2_eq, comparator_3_eq, comparator_4_eq,
       comparator_5_eq, comparator_6_eq, comparator_7_eq, comparator_8_eq, even_parity_1_out, j_k_ff_1_q,
       j_k_ff_2_q, not_1_out;

  not even_parity_1 (even_parity_1_out, in_3);  // Even_Parity
  Comparator #(.mode("unsigned")) comparator_1 (.a(in_2), .b(8'hf1), .eq(comparator_1_eq));  // open: gt, lt
  Comparator #(.mode("unsigned")) comparator_2 (.a(in_2), .b(8'h8f), .eq(comparator_2_eq));  // open: gt, lt
  Comparator #(.mode("unsigned")) comparator_3 (.a(8'hab), .b(in_2), .eq(comparator_3_eq));  // open: gt, lt
  Comparator #(.mode("unsigned")) comparator_4 (.a(8'hd5), .b(in_4), .eq(comparator_4_eq));  // open: gt, lt
  Comparator #(.mode("unsigned")) comparator_5 (.a(8'hf1), .b(in_4), .eq(comparator_5_eq));  // open: gt, lt
  Comparator #(.mode("unsigned")) comparator_6 (.a(8'hd5), .b(in_2), .eq(comparator_6_eq));  // open: gt, lt
  Comparator #(.mode("unsigned")) comparator_7 (.a(8'hab), .b(in_4), .eq(comparator_7_eq));  // open: gt, lt
  Comparator #(.mode("unsigned")) comparator_8 (.a(8'h8f), .b(in_4), .eq(comparator_8_eq));  // open: gt, lt
  or or_1 (out_5, comparator_1_eq, comparator_2_eq);
  J_K_Flip_Flop j_k_ff_1 (
    .J(comparator_3_eq), .clk(in_1), .K(comparator_3_eq), .Q(j_k_ff_1_q), .reset(comparator_4_eq));  // open: Qn, preset, en
  J_K_Flip_Flop j_k_ff_2 (
    .J(comparator_6_eq), .clk(in_1), .K(comparator_6_eq), .Q(j_k_ff_2_q), .reset(comparator_7_eq));  // open: Qn, preset, en
  not not_1 (not_1_out, even_parity_1_out);
  and and_1 (and_1_out, j_k_ff_1_q, not_1_out);
  and and_2 (and_2_out, j_k_ff_2_q, even_parity_1_out);
  or or_2 (out_6, and_1_out, comparator_5_eq);
  or or_3 (out_7, comparator_8_eq, and_2_out);
endmodule

module Generador_Random (
  input  in_1,
  output [7:0] out_2
);

  wire comparator_1_eq, demultiplexer_1_out0, demultiplexer_1_out1, random_1_out;
  wire [2:0] counter_2_q, counter_3_q;
  wire [3:0] counter_1_q, register_1_q;
  wire [7:0] rom_1_data, rom_3_data;

  Counter #(.width(4), .max('hf)) counter_1 (.Q(counter_1_q), .clk(in_1));  // open: load, D, count, carry, clr
  Register #(.width(4)) register_1 (.Q(register_1_q));  // open: D, en, clk, clr
  Counter #(.width(3), .max('h7), .ongoal("stay")) counter_2 (
    .Q(counter_2_q), .clk(in_1), .clr(comparator_1_eq));  // open: load, D, count, carry
  Comparator #(.width(4)) comparator_1 (.a(counter_1_q), .b(register_1_q), .eq(comparator_1_eq));  // open: gt, lt
  Random #(.width(1)) random_1 (.clk(comparator_1_eq), .out(random_1_out));  // open: next, clr
  Counter #(.width(3), .max('h7)) counter_3 (.Q(counter_3_q), .clk(in_1));  // open: load, D, count, carry, clr
  Demultiplexer demultiplexer_1 (
    .out0(demultiplexer_1_out0), .out1(demultiplexer_1_out1), .in(1'b1), .sel(random_1_out));  // open: en
  ROM #(.addrWidth(3)) rom_1 (.addr(counter_2_q), .data(rom_1_data), .sel(demultiplexer_1_out0));
  ROM #(.addrWidth(3)) rom_2 (.addr(counter_2_q), .data(rom_1_data), .sel(demultiplexer_1_out1));
  ROM #(.addrWidth(3)) rom_3 (.addr(counter_3_q), .data(rom_3_data));  // open: sel
  Adder adder_1 (.a(rom_1_data), .b(rom_3_data), .out(out_2));  // open: cin, cout

  // Notes on the sheet:
  //   contents of rom_1 (hex, n*v repeats v):
  //   0 50 20 70 20
  //   contents of rom_2 (hex, n*v repeats v):
  //   0 a 4 e 4
  //   contents of rom_3 (hex, n*v repeats v):
  //   81 81 81 0 81 81 81
endmodule

module Main (
  input  MOVER_AUTO
);

  wire choques_1_out_5, choques_1_out_6, choques_1_out_7, clock_1_out, controlled_buffer_1_out, nor_1_out,
       reloj_1_out_3, reloj_1_out_4, reloj_1_out_5, reloj_1_out_6, reloj_1_out_7, reloj_1_out_8,
       reloj_1_out_9, reloj_1_out_10, reloj_1_out_11, reloj_1_out_12, reloj_1_out_13, reloj_1_out_14,
       reloj_1_out_15, reloj_1_out_16, reloj_1_out_17, reloj_1_out_18, reloj_1_out_19, reloj_1_out_20,
       reloj_1_out_21, reloj_1_out_22, reloj_1_out_23, score_1_out_4, score_1_out_5, score_1_out_6,
       score_1_out_7, score_1_out_8;
  wire [7:0] generador_random_1_out_2, grupo_registros_1_out_4, grupo_registros_1_out_5,
       grupo_registros_1_out_6, grupo_registros_1_out_7, grupo_registros_1_out_8, grupo_registros_1_out_9,
       grupo_registros_1_out_10, grupo_registros_1_out_11, grupo_registros_1_out_12,
       grupo_registros_1_out_13, grupo_registros_1_out_14, grupo_registros_1_out_15,
       grupo_registros_1_out_16, grupo_registros_1_out_17, movimiento_auto_1_out_6, movimiento_auto_1_out_7,
       movimiento_auto_1_out_8, movimiento_auto_1_out_9;

  Clock clock_1 (.out(clock_1_out));
  assign controlled_buffer_1_out = nor_1_out ? clock_1_out : 1'bz;  // Controlled_Buffer controlled_buffer_1
  Reloj reloj_1 (
    .out_15(reloj_1_out_15), .out_16(reloj_1_out_16), .out_17(reloj_1_out_17), .out_18(reloj_1_out_18),
    .out_19(reloj_1_out_19), .out_20(reloj_1_out_20), .out_21(reloj_1_out_21), .out_22(reloj_1_out_22),
    .out_23(reloj_1_out_23), .out_3(reloj_1_out_3), .out_4(reloj_1_out_4), .out_5(reloj_1_out_5),
    .out_6(reloj_1_out_6), .out_7(reloj_1_out_7), .out_8(reloj_1_out_8), .out_9(reloj_1_out_9),
    .out_10(reloj_1_out_10), .out_11(reloj_1_out_11), .out_12(reloj_1_out_12), .out_13(reloj_1_out_13),
    .out_14(reloj_1_out_14), .in_2(controlled_buffer_1_out), .in_1(nor_1_out));
  _7_Segment_Display u_7_segment_display_1 (
    .g(reloj_1_out_3), .f(reloj_1_out_4), .a(reloj_1_out_5), .b(reloj_1_out_6), .e(reloj_1_out_15),
    .d(reloj_1_out_16), .c(reloj_1_out_17));  // open: dp
  LED led_1 (.in(1'b1));
  LED led_2 (.in(1'b1));
  Generador_Random generador_random_1 (.in_1(controlled_buffer_1_out), .out_2(generador_random_1_out_2));
  _7_Segment_Display u_7_segment_display_2 (
    .g(reloj_1_out_7), .f(reloj_1_out_8), .a(reloj_1_out_9), .b(reloj_1_out_10), .e(reloj_1_out_18),
    .d(reloj_1_out_19), .c(reloj_1_out_20));  // open: dp
  _7_Segment_Display u_7_segment_display_3 (
    .g(reloj_1_out_11), .f(reloj_1_out_12), .a(reloj_1_out_13), .b(reloj_1_out_14), .e(reloj_1_out_21),
    .d(reloj_1_out_22), .c(reloj_1_out_23));  // open: dp
  Grupo_Registros grupo_registros_1 (
    .in_1(generador_random_1_out_2), .in_2(controlled_buffer_1_out), .out_4(grupo_registros_1_out_4),
    .out_5(grupo_registros_1_out_5), .out_6(grupo_registros_1_out_6), .out_7(grupo_registros_1_out_7),
    .out_8(grupo_registros_1_out_8), .out_9(grupo_registros_1_out_9), .out_10(grupo_registros_1_out_10),
    .out_11(grupo_registros_1_out_11), .out_12(grupo_registros_1_out_12), .out_13(grupo_registros_1_out_13),
    .out_14(grupo_registros_1_out_14), .out_15(grupo_registros_1_out_15), .out_16(grupo_registros_1_out_16),
    .out_17(grupo_registros_1_out_17));  // open: in_3
  Movimiento_auto movimiento_auto_1 (
    .out_6(movimiento_auto_1_out_6), .out_7(movimiento_auto_1_out_7), .out_8(movimiento_auto_1_out_8),
    .out_9(movimiento_auto_1_out_9), .in_1(MOVER_AUTO), .in_3(grupo_registros_1_out_15),
    .in_4(grupo_registros_1_out_16), .in_2(grupo_registros_1_out_14), .in_5(grupo_registros_1_out_17));
  LED led_3 (.in(score_1_out_5));
  LED led_4 (.in(score_1_out_8));
  LED led_5 (.in(score_1_out_6));
  LED led_6 (.in(score_1_out_7));
  Score score_1 (
    .in_1(movimiento_auto_1_out_9), .in_2(controlled_buffer_1_out), .out_4(score_1_out_4),
    .out_5(score_1_out_5), .out_6(score_1_out_6), .out_7(score_1_out_7), .out_8(score_1_out_8),
    .in_3(nor_1_out));
  LED led_7 (.in(score_1_out_4));
  Choques choques_1 (
    .in_2(movimiento_auto_1_out_6), .out_5(choques_1_out_5), .in_4(movimiento_auto_1_out_9),
    .out_6(choques_1_out_6), .out_7(choques_1_out_7), .in_1(controlled_buffer_1_out), .in_3(MOVER_AUTO));
  nor nor_1 (nor_1_out, choques_1_out_5, choques_1_out_6, choques_1_out_7);
  DotMatrix #(.inputtype("row"), .matrixcols(8), .matrixrows(16)) dotmatrix_1 (
    .row0(generador_random_1_out_2), .row1(grupo_registros_1_out_4), .row2(grupo_registros_1_out_5),
    .row3(grupo_registros_1_out_6), .row4(grupo_registros_1_out_7), .row5(grupo_registros_1_out_8),
    .row6(grupo_registros_1_out_9), .row7(grupo_registros_1_out_10), .row8(grupo_registros_1_out_11),
    .row9(grupo_registros_1_out_12), .row10(grupo_registros_1_out_13), .row11(movimiento_auto_1_out_6),
    .row12(movimiento_auto_1_out_7), .row13(movimiento_auto_1_out_8), .row14(movimiento_auto_1_out_9));  // open: row15

  // Notes on the sheet:
  //   Score:
endmodule

module Reloj (
  input  in_1,
  input  in_2,
  output out_3,
  output out_4,
  output out_5,
  output out_6,
  output out_7,
  output out_8,
  output out_9,
  output out_10,
  output out_11,
  output out_12,
  output out_13,
  output out_14,
  output out_15,
  output out_16,
  output out_17,
  output out_18,
  output out_19,
  output out_20,
  output out_21,
  output out_22,
  output out_23
);

  Reloj_circ_principal reloj_circ_principal_1 (
    .Clock(in_2), .a3(out_5), .b3(out_6), .c3(out_17), .d3(out_16), .e3(out_15), .f3(out_4), .g3(out_3),
    .a2(out_9), .b2(out_10), .c2(out_20), .d2(out_19), .e2(out_18), .f2(out_8), .g2(out_7), .a1(out_13),
    .b1(out_14), .c1(out_23), .d1(out_22), .e1(out_21), .f1(out_12), .g1(out_11), .in_1(in_1));
endmodule

module Reloj_circ_principal (
  input  in_1,
  input  Clock,
  output a3,
  output b3,
  output c3,
  output d3,
  output e3,
  output f3,
  output g3,
  output a2,
  output b2,
  output c2,
  output d2,
  output e2,
  output f2,
  output g2,
  output a1,
  output b1,
  output c1,
  output d1,
  output e1,
  output f1,
  output g1
);

  wire and_1_out, and_2_out, reloj_comp1_1_q1, reloj_comp1_1_q2, reloj_comp1_1_q3, reloj_comp1_1_q4,
       reloj_comp1_2_q1, reloj_comp1_2_q2, reloj_comp1_2_q3, reloj_comp1_2_q4, reloj_comp2_1_q1,
       reloj_comp2_1_q2, reloj_comp2_1_q3, reloj_comp2_1_q4;

  Reloj_comp0 reloj_comp0_1 (
    .x1(reloj_comp1_1_q1), .x2(reloj_comp1_1_q2), .x3(reloj_comp1_1_q3), .x4(reloj_comp1_1_q4), .a(a3),
    .b(b3), .c(c3), .d(d3), .e(e3), .f(f3), .g(g3));
  Reloj_comp1 reloj_comp1_1 (
    .clock(Clock), .clock_2(and_1_out), .in_3(in_1), .Q4(reloj_comp1_1_q4), .Q3(reloj_comp1_1_q3),
    .Q2(reloj_comp1_1_q2), .Q1(reloj_comp1_1_q1));
  and and_1 (and_1_out, reloj_comp2_1_q2, reloj_comp2_1_q3);
  Reloj_comp0 reloj_comp0_2 (
    .x1(reloj_comp2_1_q1), .x2(reloj_comp2_1_q2), .x3(reloj_comp2_1_q3), .x4(reloj_comp2_1_q4), .a(a2),
    .b(b2), .c(c2), .d(d2), .e(e2), .f(f2), .g(g2));
  Reloj_comp2 reloj_comp2_1 (
    .clock(Clock), .pause(and_2_out), .in_3(in_1), .Q4(reloj_comp2_1_q4), .Q3(reloj_comp2_1_q3),
    .Q2(reloj_comp2_1_q2), .Q1(reloj_comp2_1_q1));
  and and_2 (and_2_out, reloj_comp1_2_q3, reloj_comp1_2_q1);
  Reloj_comp0 reloj_comp0_3 (
    .x1(reloj_comp1_2_q1), .x2(reloj_comp1_2_q2), .x3(reloj_comp1_2_q3), .x4(reloj_comp1_2_q4), .a(a1),
    .b(b1), .c(c1), .d(d1), .e(e1), .f(f1), .g(g1));
  Reloj_comp1 reloj_comp1_2 (
    .clock(Clock), .clock_2(1'b1), .in_3(in_1), .Q4(reloj_comp1_2_q4), .Q3(reloj_comp1_2_q3),
    .Q2(reloj_comp1_2_q2), .Q1(reloj_comp1_2_q1));
endmodule

module Reloj_comp0 (
  input  x1,
  input  x2,
  input  x3,
  input  x4,
  output a,
  output b,
  output c,
  output d,
  output e,
  output f,
  output g
);

  wire and_1_out, and_2_out, and_3_out, and_4_out, and_5_out, and_6_out, and_7_out, and_8_out, and_9_out,
       and_10_out, and_11_out, and_12_out, and_13_out, and_14_out, and_15_out, and_16_out, not_1_out,
       not_2_out, not_3_out, not_4_out, not_5_out, not_6_out, not_7_out, not_8_out, not_9_out, not_10_out,
       not_11_out, not_12_out, not_13_out, not_14_out, not_15_out, not_16_out, not_17_out, not_18_out,
       not_19_out, not_20_out, not_21_out;

  not not_1 (not_1_out, x2);
  and and_1 (and_1_out, not_1_out, not_2_out);
  not not_2 (not_2_out, x4);
  and and_2 (and_2_out, x2, x4);
  not not_3 (not_3_out, x2);
  not not_4 (not_4_out, x3);
  and and_3 (and_3_out, not_4_out, not_5_out);
  not not_5 (not_5_out, x4);
  and and_4 (and_4_out, x3, x4);
  not not_6 (not_6_out, x3);
  or or_1 (c, not_6_out, x4, x2);
  not not_7 (not_7_out, x2);
  and and_5 (and_5_out, not_7_out, not_8_out);
  not not_8 (not_8_out, x4);
  not not_9 (not_9_out, x2);
  and and_6 (and_6_out, not_9_out, x3);
  and and_7 (and_7_out, x3, not_10_out);
  not not_10 (not_10_out, x4);
  and and_8 (and_8_out, x2, not_11_out, x4);
  not not_11 (not_11_out, x3);
  not not_12 (not_12_out, x2);
  and and_9 (and_9_out, not_12_out, not_13_out);
  not not_13 (not_13_out, x4);
  and and_10 (and_10_out, x3, not_14_out);
  not not_14 (not_14_out, x4);
  not not_15 (not_15_out, x3);
  and and_11 (and_11_out, not_15_out, not_16_out);
  not not_16 (not_16_out, x4);
  and and_12 (and_12_out, x2, not_17_out);
  not not_17 (not_17_out, x3);
  and and_13 (and_13_out, x2, not_18_out);
  not not_18 (not_18_out, x4);
  not not_19 (not_19_out, x2);
  and and_14 (and_14_out, not_19_out, x3);
  and and_15 (and_15_out, x2, not_20_out);
  not not_20 (not_20_out, x3);
  and and_16 (and_16_out, x2, not_21_out);
  not not_21 (not_21_out, x4);
  or or_2 (a, and_1_out, x3, and_2_out, x1);
  or or_3 (b, not_3_out, and_3_out, and_4_out);
  or or_4 (d, and_5_out, and_6_out, and_7_out, and_8_out, x1);
  or or_5 (e, and_9_out, and_10_out);
  or or_6 (f, and_11_out, and_12_out, and_13_out, x1);
  or or_7 (g, and_14_out, and_15_out, and_16_out, x1);
endmodule

module Reloj_comp1 (
  input  clock,
  input  clock_2,
  input  in_3,
  output Q4,
  output Q3,
  output Q2,
  output Q1
);

  wire and_1_out, and_2_out, and_3_out, and_4_out, multiplexer_1_out, multiplexer_2_out, multiplexer_3_out;

  J_K_Flip_Flop j_k_ff_1 (
    .J(1'b1), .clk(and_1_out), .K(1'b1), .Q(Q4), .reset(multiplexer_1_out));  // open: Qn, preset, en
  and and_1 (and_1_out, clock, clock_2);
  Multiplexer multiplexer_1 (.in0(1'b1), .in1(and_4_out), .out(multiplexer_1_out), .sel(in_3));  // open: en
  and and_2 (and_2_out, Q4, Q3);
  J_K_Flip_Flop j_k_ff_2 (.J(Q4), .clk(and_1_out), .K(Q4), .Q(Q3), .reset(multiplexer_1_out));  // open: Qn, preset, en
  and and_3 (and_3_out, and_2_out, Q2);
  J_K_Flip_Flop j_k_ff_3 (
    .J(and_2_out), .clk(and_1_out), .K(and_2_out), .Q(Q2), .reset(multiplexer_2_out));  // open: Qn, preset, en
  Multiplexer multiplexer_2 (.in0(1'b1), .in1(and_4_out), .out(multiplexer_2_out), .sel(in_3));  // open: en
  J_K_Flip_Flop j_k_ff_4 (
    .J(and_3_out), .clk(and_1_out), .K(and_3_out), .Q(Q1), .reset(multiplexer_3_out));  // open: Qn, preset, en
  Multiplexer multiplexer_3 (.in0(1'b1), .in1(and_4_out), .out(multiplexer_3_out), .sel(in_3));  // open: en
  and and_4 (and_4_out, Q1, Q3);
endmodule

module Reloj_comp2 (
  input  clock,
  input  pause,
  input  in_3,
  output Q4,
  output Q3,
  output Q2,
  output Q1
);

  wire and_1_out, and_2_out, and_3_out, and_4_out, multiplexer_1_out, multiplexer_2_out, multiplexer_3_out;

  and and_1 (and_1_out, clock, pause);
  J_K_Flip_Flop j_k_ff_1 (
    .J(1'b1), .clk(and_1_out), .K(1'b1), .Q(Q4), .reset(multiplexer_1_out));  // open: Qn, preset, en
  and and_2 (and_2_out, Q4, Q3);
  J_K_Flip_Flop j_k_ff_2 (.J(Q4), .clk(and_1_out), .K(Q4), .Q(Q3), .reset(multiplexer_1_out));  // open: Qn, preset, en
  Multiplexer multiplexer_1 (.in0(1'b1), .in1(and_4_out), .out(multiplexer_1_out), .sel(in_3));  // open: en
  J_K_Flip_Flop j_k_ff_3 (
    .J(and_2_out), .clk(and_1_out), .K(and_2_out), .Q(Q2), .reset(multiplexer_2_out));  // open: Qn, preset, en
  Multiplexer multiplexer_2 (.in0(1'b1), .in1(and_4_out), .out(multiplexer_2_out), .sel(in_3));  // open: en
  and and_3 (and_3_out, and_2_out, Q2);
  J_K_Flip_Flop j_k_ff_4 (
    .J(and_3_out), .clk(and_1_out), .K(and_3_out), .Q(Q1), .reset(multiplexer_3_out));  // open: Qn, preset, en
  Multiplexer multiplexer_3 (.in0(1'b1), .in1(and_4_out), .out(multiplexer_3_out), .sel(in_3));  // open: en
  and and_4 (and_4_out, Q2, Q3);
endmodule
